// Logisim project logisim_micro_demo.circ as structural Verilog: 1 circuit, main circuit main
module main (
);

  wire button_1_out, button_2_out, button_3_out, button_4_out, button_5_out, button_6_out, clock_1_out,
       multiplexer_1_out, por_1_out;
  wire [3:0] rom_1_data, rom_1_data_2, rom_1_data_3, rom_1_data_4, rom_1_data_5;
  wire [7:0] counter_1_q;

  Button button_1 (.out(button_1_out));
  Button button_2 (.out(button_2_out));
  Button button_3 (.out(button_3_out));
  Button button_4 (.out(button_4_out));
  Button button_5 (.out(button_5_out));
  Button button_6 (.out(button_6_out));
  Multiplexer #(.enable("false"), .select(3)) multiplexer_1 (
    .in0(1'b0), .in1(button_1_out), .in2(button_2_out), .in3(button_3_out), .in4(button_4_out),
    .in5(button_5_out), .in6(button_6_out), .in7(1'b1), .out(multiplexer_1_out), .sel(rom_1_data_3[2:0]));
  Clock clock_1 (.out(clock_1_out));
  POR por_1 (.out(por_1_out));
  Counter counter_1 (
    .clr(por_1_out), .load(multiplexer_1_out), .up(1'b1), .clk(clock_1_out), .D({rom_1_data_2, rom_1_data}),
    .Q(counter_1_q));  // open: count, carry
  Hex_Digit_Display hex_digit_display_1 (.value(counter_1_q[7:4]));  // open: dp
  ROM #(.dataWidth(20)) rom_1 (
    .addr(counter_1_q), .data({rom_1_data_2, rom_1_data, rom_1_data_5, rom_1_data_4, rom_1_data_3}));
  Hex_Digit_Display hex_digit_display_2 (.value(counter_1_q[3:0]));  // open: dp
  LED led_1 (.in(rom_1_data_5[3]));
  LED led_2 (.in(rom_1_data_5[2]));
  LED led_3 (.in(rom_1_data_5[1]));
  LED led_4 (.in(rom_1_data_5[0]));
  LED led_5 (.in(rom_1_data_4[3]));
  LED led_6 (.in(rom_1_data_4[2]));
  LED led_7 (.in(rom_1_data_4[1]));
  LED led_8 (.in(rom_1_data_4[0]));

  // Notes on the sheet:
  //   contents of rom_1 (hex, n*v repeats v):
  //   0 800 400 200 100 80 40 20 10 21001 22002 23003 24004 25005 26006 7 17*0 31117 32227 33337 34447
  //   35557 36667 10*0 41117 42227 43337 44447 45557 46667 10*0 51117 52227 53337 54447 55557 56667 10*0
  //   117 227 337 447 557 667
endmodule
